// Logisim project 16bit_ALU.circ as structural Verilog: 4 circuits, main circuit main
module main (
  input  [15:0] A,
  input  [15:0] B,
  input  [2:0] Select_Operation,
  input  Reset
);
endmodule

module FullAdder (
  input  A,
  input  B,
  input  Cin,
  output Sum,
  output Cout
);

  wire and_1_out, and_2_out, xor_1_out;

  xor xor_1 (xor_1_out, A, B);
  xor xor_2 (Sum, xor_1_out, Cin);
  and and_1 (and_1_out, Cin, xor_1_out);
  and and_2 (and_2_out, A, B);
  or or_1 (Cout, and_1_out, and_2_out);
endmodule

module Adder4 (
  input  Cin,
  input  [3:0] A,
  input  [3:0] B,
  output [3:0] Sum,
  output Cout
);

  wire fa1_cout, fa2_cout, fa3_cout;

  FullAdder fa1 (.A(A[0]), .B(B[0]), .Cin(Cin), .Sum(Sum[0]), .Cout(fa1_cout));
  FullAdder fa2 (.A(A[1]), .B(B[1]), .Cin(fa1_cout), .Sum(Sum[1]), .Cout(fa2_cout));
  FullAdder fa3 (.A(A[2]), .B(B[2]), .Cin(fa2_cout), .Sum(Sum[2]), .Cout(fa3_cout));
  FullAdder fa4 (.A(A[3]), .B(B[3]), .Cin(fa3_cout), .Sum(Sum[3]), .Cout(Cout));
endmodule

// Sum
module Adder16 (
  input  Cin,
  input  [15:0] A,
  input  [15:0] B,
  output [15:0] Sum,
  output Cout
);

  wire adder4_1_cout, adder4_2_cout, adder4_3_cout;

  Adder4 adder4_1 (.Cin(Cin), .A(A[3:0]), .B(B[3:0]), .Sum(Sum[3:0]), .Cout(adder4_1_cout));
  Adder4 adder4_2 (.Cin(adder4_1_cout), .A(A[7:4]), .B(B[7:4]), .Sum(Sum[7:4]), .Cout(adder4_2_cout));
  Adder4 adder4_3 (.Cin(adder4_2_cout), .A(A[11:8]), .B(B[11:8]), .Sum(Sum[11:8]), .Cout(adder4_3_cout));
  Adder4 adder4_4 (.Cin(adder4_3_cout), .A(A[15:12]), .B(B[15:12]), .Sum(Sum[15:12]), .Cout(Cout));
endmodule
